# Fritzing sketch LDR (saved by Fritzing 0.9.3b)
breadboards: 1

parts:
  Componente1 = Arduino Uno (Rev3)
  R1 = Photocell (LDR) [package=THT]
  R2 = Resistor [tolerance=±5% resistance=10k package=THT]
  R3 = Resistor [tolerance=±5% resistance=150 package=THT]
  LED1 = LED - 3mm [color="Red (633nm)" package="3 mm [THT]"]

nets:
  N1: Componente1.A5/SCL, R1.pin_1, R2.Pin_0
  N2: Componente1.D10_PWM/SS, R3.Pin_1
  N3: Componente1.GND, R1.pin_0, LED1.cathode
  N4: Componente1.5V, R2.Pin_1
  N5: R3.Pin_0, LED1.anode
