# Fritzing sketch infraRed (saved by Fritzing 0.9.3b)
breadboards: 1

parts:
  Componente1 = Arduino Uno (Rev3)
  IR1 = TSOP312.., 314.. [package=THT]
  R1 = Resistor [tolerance=±5% resistance=150 package=THT]
  R2 = Resistor [tolerance=±5% resistance=150 package=THT]
  R3 = Resistor [tolerance=±5% resistance=150 package=THT]
  LED1 = LED - 5mm [color="Red (633nm)" package="5 mm [THT]"]
  LED2 = LED - 5mm [color="Red (633nm)" package="5 mm [THT]"]
  LED3 = LED - 5mm [color="Red (633nm)" package="5 mm [THT]"]

nets:
  N1: Componente1.D8, R1.Pin_1
  N2: Componente1.D9_PWM, R3.Pin_1
  N3: Componente1.D10_PWM/SS, R2.Pin_1
  N4: Componente1.D2, IR1.GND
  N5: Componente1.5V, IR1.Data
  N6: Componente1.GND, IR1.Vs, LED1.cathode, LED2.cathode, LED3.cathode
  N7: R1.Pin_0, LED3.anode
  N8: R2.Pin_0, LED1.anode
  N9: R3.Pin_0, LED2.anode
