# Fritzing sketch ledsComSenhat (saved by Fritzing 0.9.3b)
breadboards: 1

parts:
  Componente1 = Arduino Uno (Rev3)
  R1 = Resistor [tolerance=±5% resistance=150 package=THT]
  LED1 = LED - 5mm [color="Red (633nm)" current=1.8 package="5 mm [THT]"]
  LED2 = LED - 5mm [color="Green (555nm)" current=1.8 package="5 mm [THT]"]
  R2 = Resistor [tolerance=±5% resistance=150 package=THT]
  S1 = Pushbutton [package="[THT]"]

nets:
  N1: Componente1.D8, R2.Pin_0
  N2: Componente1.D12/MISO, S1.Pin_3, S1.Pin_4
  N3: Componente1.D13/SCK, R1.Pin_0
  N4: Componente1.GND, LED1.cathode, LED2.cathode, S1.Pin_1, S1.Pin_2
  N5: R1.Pin_1, LED1.anode
  N6: LED2.anode, R2.Pin_1

// code stored in the sketch: ledsComSenhat.ino
  const int led = 13;
  const int led2 = 8;
  const int button = 12;
  bool looping = true;
  int logi = 0;
void teste(){
  while(looping){
    if(Serial.read() == '1'){
      logi = 1;
      Serial.println("vermelho");
      looping = false;
    }
    else if(Serial.read() == '2'){
      logi = 2;
      Serial.println("verde/amarelo");
      looping = false;
    }
        
    else if(Serial.read() == '3'){
      logi = 3;
      Serial.println("ambos");
      looping = false;
      
    }  
  }
}
void setup() {
  pinMode(led, OUTPUT);
  pinMode(button, INPUT_PULLUP);
  pinMode(led2, OUTPUT);
  Serial.begin(9600);
  digitalWrite(led, LOW);
}

void loop() {
  delay(1000);
  Serial.println("1-Led vermelho; 2-Led verde/amarelo; 3-ambos Leds; após selecionado aperte 't' para selecionar nova cor");
  looping = true;
  teste();



  
    while(logi==1){
     if(digitalRead(button) == LOW){
       digitalWrite(led, HIGH);
     }
     else{
       digitalWrite(led, LOW);
     }
     if (Serial.read() == 't'){ 
       Serial.println("1-Led vermelho; 2-Led verde/amarelo; 3-ambos Leds;"); 
       looping = true;
       teste();
     }
   }






   while(logi==2){
     if(digitalRead(button) == LOW){
       digitalWrite(led2, HIGH);
     }
     else{
       digitalWrite(led2, LOW);
     }
     if(Serial.read() == 't'){
       Serial.println("1-Led vermelho; 2-Led verde/amarelo; 3-ambos Leds;");
       looping = true;
       teste();
     }
   }

  







  

   while(logi==3){
     if(digitalRead(button) == LOW){
       digitalWrite(led, HIGH);
       digitalWrite(led2, HIGH);
     }
     else{
       digitalWrite(led, LOW);
       digitalWrite(led2, LOW);
     }
     if(Serial.read() == 't'){
       Serial.println("1-Led vermelho; 2-Led verde/amarelo; 3-ambos Leds;");  
       looping = true;
       teste();
     }
   }


}
