# Fritzing sketch num (saved by Fritzing 0.9.3b)
breadboards: 1

parts:
  Componente1 = Arduino Uno (Rev3)
  R1 = Resistor [tolerance=±5% resistance=220 package=THT]
  R2 = Resistor [tolerance=±5% resistance=220 package=THT]
  R3 = Resistor [tolerance=±5% resistance=220 package=THT]
  R4 = Resistor [tolerance=±5% resistance=220 package=THT]
  R5 = Resistor [tolerance=±5% resistance=220 package=THT]
  R6 = Resistor [tolerance=±5% resistance=220 package=THT]
  R7 = Resistor [tolerance=±5% resistance=220 package=THT]
  R8 = Resistor [tolerance=±5% resistance=220 package=THT]
  DI1 = 7-Segment LED Display [package=THT]

nets:
  N1: Componente1.D8, R4.Pin_0
  N2: Componente1.D9_PWM, R8.Pin_1
  N3: Componente1.D2, R6.Pin_1
  N4: Componente1.D3_PWM, R5.Pin_1
  N5: Componente1.D4, R2.Pin_1
  N6: Componente1.D5_PWM, R7.Pin_0
  N7: Componente1.D6_PWM, R3.Pin_0
  N8: Componente1.D7, R1.Pin_0
  N9: Componente1.5V, DI1.commAnode#7
  N10: R1.Pin_1, DI1.cathodeF
  N11: R2.Pin_0, DI1.cathodeC
  N12: R3.Pin_1, DI1.cathodeE
  N13: R4.Pin_1, DI1.cathodeG
  N14: R5.Pin_0, DI1.cathodeB
  N15: R6.Pin_0, DI1.cathodeA
  N16: R7.Pin_1, DI1.cathodeD
  N17: R8.Pin_0, DI1.cathodeDP
