# Fritzing sketch potenci (saved by Fritzing 0.9.3b)
breadboards: 1

parts:
  Componente1 = Arduino Uno (Rev3)
  LED1 = LED - 3mm [color="Red (633nm)" package="3 mm [THT]"]
  LED2 = LED - 3mm [color="Yellow (595nm)" package="3 mm [THT]"]
  R1 = Resistor [tolerance=±5% resistance=150 package=THT]
  R2 = Resistor [tolerance=±5% resistance=150 package=THT]
  R3 = Resistor [tolerance=±5% resistance=150 package=THT]
  LED3 = LED - 3mm [color="Green (555nm)" package="3 mm [THT]"]
  U1 = POT [package=pot_alpha_rv16af-20]

nets:
  N1: Componente1.A5/SCL, U1.S
  N2: Componente1.D8, R1.Pin_1
  N3: Componente1.D12/MISO, R2.Pin_0
  N4: Componente1.D13/SCK, R3.Pin_1
  N5: Componente1.5V, U1.A
  N6: Componente1.GND, LED1.cathode, LED2.cathode, LED3.cathode, U1.E
  N7: LED1.anode, R3.Pin_0
  N8: LED2.anode, R2.Pin_1
  N9: R1.Pin_0, LED3.anode
