# Fritzing sketch ultra (saved by Fritzing 0.9.3b)
breadboards: 1

parts:
  Componente1 = Arduino Uno (Rev3)
  hc-sr1 = hc-sr04
  LED1 = smd LED [color="Red (633nm)" package="0805 [SMD]"]
  R1 = Resistor [tolerance=±5% resistance=220 package="2010 [SMD]"]

nets:
  N1: Componente1.D8, hc-sr1.Trig
  N2: Componente1.D9_PWM, hc-sr1.Echo
  N3: Componente1.D10_PWM/SS, R1.Pin_1
  GND: Componente1.GND, hc-sr1.GND, LED1.cathode
  5V: Componente1.5V, hc-sr1.VCC
  N4: LED1.anode, R1.Pin_0
